# Fritzing sketch Placa PCB - CHAQUETON (saved by Fritzing 0.9.3b)
circuit board: 6.92923cm x 4.20388cm
breadboards: 1

parts:
  WeMos_D1_Mini1 = WeMos D1 Mini
  LED1 = LED - 5mm [color="Red (633nm)" package="5 mm [THT]"]
  RHT1 = Humidity and Temperature Sensor RHT03
  SEN1 = Pulse Sensor [package=SIP]
  HC-SR04_Sensor_1 = HC-SR04 Ultrasonic Distance Sensor
  GY-NEO6MV3 = SUP500F [package=sup500f]
  J1 = Piezo Speaker
  U1 = Graphical LCD 128x64 [package=lcd-g12864]
  R1 = Resistor [tolerance=±5% resistance=330 package=THT]

nets:
  VCC: WeMos_D1_Mini1.5V, LED1.cathode, RHT1.Vcc, SEN1.Vcc, HC-SR04_Sensor_1.VCC, GY-NEO6MV3.TX-O, J1.pin2
  N1: WeMos_D1_Mini1.D3, R1.Pin_1
  N2: WeMos_D1_Mini1.D4, HC-SR04_Sensor_1.ECHO
  N3: WeMos_D1_Mini1.D5, HC-SR04_Sensor_1.TRIG
  N4: WeMos_D1_Mini1.D6, RHT1.Data-signal
  N5: WeMos_D1_Mini1.D7, SEN1.Signal
  GND: WeMos_D1_Mini1.G, RHT1.GND_2, SEN1.GND, HC-SR04_Sensor_1.GND, GY-NEO6MV3.RX-I, J1.pin1, U1.VSS, U1.VO, U1.DB0, U1.DB1, U1.DB2, U1.DB4, U1.DB5, U1.DB6, U1.DB7, U1.CS2, U1.RST, U1.R_W, U1.D_I, U1.E, U1.VEE, U1.K
  N6: LED1.anode, R1.Pin_0

custom parts:
  Pulse Sensor: Pulse Sensor Optical Heart Rate Monitor for Arduino and other microcontrollers
